# Fritzing sketch Montage_Coeur (saved by Fritzing 0.9.3b)
breadboards: 1

parts:
  part = Resistor [tolerance=±5% resistance=220 package=THT]
  R2 = Resistor [tolerance=±5% resistance=220 package=THT]
  R3 = Resistor [tolerance=±5% resistance=220 package=THT]
  R4 = Resistor [tolerance=±5% resistance=220 package=THT]
  R5 = Resistor [tolerance=±5% resistance=220 package=THT]
  R6 = Resistor [tolerance=±5% resistance=220 package=THT]
  R7 = Resistor [tolerance=±5% resistance=220 package=THT]
  R8 = Resistor [tolerance=±5% resistance=220 package=THT]
  R9 = Resistor [tolerance=±5% resistance=220 package=THT]
  R6_2 = Resistor [tolerance=±5% resistance=220 package=THT]
  LED3 = LED - 5mm [color="Red (633nm)" package="5 mm [THT]"]
  LED4 = LED - 5mm [color="Red (633nm)" package="5 mm [THT]"]
  LED5 = LED - 5mm [color="Red (633nm)" package="5 mm [THT]"]
  LED6 = LED - 5mm [color="Red (633nm)" package="5 mm [THT]"]
  LED8 = LED - 5mm [color="Red (633nm)" package="5 mm [THT]"]
  LED8_2 = LED - 5mm [color="Red (633nm)" package="5 mm [THT]"]
  LED9 = LED - 5mm [color="Red (633nm)" package="5 mm [THT]"]
  LED7 = LED - 5mm [color="Red (633nm)" package="5 mm [THT]"]
  Arduino_Uno = Arduino Uno (Rev3)
  LED1 = LED - 5mm [color="Red (633nm)" package="5 mm [THT]"]
  LED2 = LED - 5mm [color="Red (633nm)" package="5 mm [THT]"]

nets:
  N1: part.Pin_0, R6.Pin_0, Arduino_Uno.D0/RX
  N2: part.Pin_1, LED1.anode
  N3: R2.Pin_0, Arduino_Uno.D1/TX
  N4: R2.Pin_1, LED2.anode
  N5: R3.Pin_0, Arduino_Uno.D2
  N6: R3.Pin_1, LED3.anode
  N7: R4.Pin_0, Arduino_Uno.D3_PWM
  N8: R4.Pin_1, LED4.anode
  N9: R5.Pin_0, Arduino_Uno.D4
  N10: R5.Pin_1, LED5.anode
  N11: R6.Pin_1, LED6.anode
  N12: R7.Pin_0, LED8.cathode
  N13: R7.Pin_1, R8.Pin_1, R6_2.Pin_1, LED3.cathode, LED4.cathode, LED5.cathode, LED6.cathode, LED8_2.cathode, LED8_2.anode, LED9.cathode, Arduino_Uno.GND, LED1.cathode, LED2.cathode
  N14: R8.Pin_0, Arduino_Uno.D8
  N15: R9.Pin_0, Arduino_Uno.D9_PWM
  N16: R9.Pin_1, LED9.anode
  N17: R6_2.Pin_0, LED7.cathode
  N18: LED8.anode, Arduino_Uno.D7
  N19: LED7.anode, Arduino_Uno.D6_PWM
