# Fritzing sketch Montage_capteur-DESKTOP-S5DREBE (saved by Fritzing 0.9.3b)
breadboards: 1

parts:
  IC1 = LM324 [package=dil16]
  R3 = Resistor [tolerance=±5% resistance=68k package=THT]
  R4 = Resistor [tolerance=±5% resistance=8.2k package=THT]
  R2 = Resistor [tolerance=±5% resistance=10k package=THT]
  R1 = Resistor [tolerance=±5% resistance=220 package=THT]
  Q1 = LTR-301 [package=ltr-301]
  LED1 = LED - 5mm [color="Red (633nm)" package="5 mm [THT]"]  # not connected
  C1 = Ceramic Capacitor [capacitance=100nF package="100 mil [THT, multilayer]"]
  C2 = Ceramic Capacitor [capacitance=1µF package="100 mil [THT, multilayer]"]
  C3 = Ceramic Capacitor [capacitance=1µF package="100 mil [THT, multilayer]"]
  R5 = Resistor [tolerance=±5% resistance=68k package=THT]
  C4 = Ceramic Capacitor [capacitance=100nF package="100 mil [THT, multilayer]"]
  R6 = Resistor [tolerance=±20% resistance=470k package=THT]
  R7 = Resistor [tolerance=±5% resistance=1.8k package=THT]
  Q2 = NPN-Transistor [package="TO92 [THT]"]
  Composant1 = Arduino Uno (Rev3)
  Q3 = LTR-301 [package=ltr-301]  # not connected

nets (from the schematic view):
  N1: IC1.OUT1, C2.1, C3.0
  N2: IC1.IN1-, R4.Pin_1, C2.0
  N3: IC1.IN1+, R3.Pin_1, C1.1
  5V: IC1.V+, R2.Pin_1, R1.Pin_1, Q2.C
  GND: IC1.GND, R3.Pin_0, R4.Pin_0, Q1.E, R5.Pin_0
  N4: IC1.IN4+, C3.1, R5.Pin_1
  N5: IC1.IN4-, C4.0, R6.Pin_1
  N6: IC1.OUT4, C4.1, R6.Pin_0, R7.Pin_0
  N7: R2.Pin_0, Q1.C, C1.0
  N8: R7.Pin_1, Q2.B
  N9: Q2.E, Composant1.A0

custom parts:
  LM324: LM324 Quad OpAmp
